// Logisim project CPU-LASER-RISCV.circ as structural Verilog: 13 circuits, main circuit DATA PATH
module DATA_PATH (
);

  wire alu_1_zero, circuit_three_1_funct7_5, clock_1_out, clock_2_out, clock_3_out, clock_4_out, clock_5_out,
       fsm_1_out_8, fsm_1_out_9, fsm_1_out_10, fsm_1_out_14, fsm_1_pcwrite, undriven_2;
  wire [1:0] fsm_1_out_11, fsm_1_out_12, fsm_1_out_13, fsm_1_out_16;
  wire [2:0] circuit_three_1_funct3_14_12, fsm_1_out_15;
  wire [4:0] circuit_three_1_out_5, circuit_three_1_out_6, circuit_three_1_rd_11_7;
  wire [6:0] circuit_three_1__6_0__op;
  wire [23:0] bit_extender_1_out;
  wire [31:0] alu_1_out_5, extend_1_out_3, multiplexer_1_out, multiplexer_2_out, multiplexer_3_out,
       multiplexer_4_out, ram_1_data, register_1_q, register_2_q, register_3_q, register_4_q, register_5_q,
       register_6_q, register_7_q, registerfile_32x32_2_read_1_write_1_out_7,
       registerfile_32x32_2_read_1_write_1_out_8, undriven;

  Register #(.width(32)) register_1 (
    .D(multiplexer_4_out), .en(fsm_1_pcwrite), .Q(register_1_q), .clk(clock_1_out), .clr(1'b0));
  Multiplexer #(.width(32), .enable("false")) multiplexer_1 (
    .in0(register_1_q), .in1(multiplexer_4_out), .out(multiplexer_1_out), .sel(fsm_1_out_14));
  Clock clock_1 (.out(clock_1_out));
  Bit_Extender #(.in_width(32), .out_width(24), .\type ("sign")) bit_extender_1 (
    .in(multiplexer_1_out), .out(bit_extender_1_out));
  // Probe on register_6_q
  RAM #(.addrWidth(24), .dataWidth(32), .bus("separate")) ram_1 (
    .addr(bit_extender_1_out), .din(register_6_q), .data(ram_1_data), .str(fsm_1_out_9), .sel(1'b1),
    .clk(clock_1_out), .ld(1'b1));  // open: clr
  Register #(.width(32)) register_2 (
    .D(register_1_q), .en(fsm_1_out_10), .Q(register_2_q), .clk(clock_1_out));  // open: clr
  Register #(.width(32)) register_3 (
    .D(ram_1_data), .en(fsm_1_out_10), .Q(register_3_q), .clk(clock_1_out));  // open: clr
  Register #(.width(32)) register_4 (.D(ram_1_data), .en(1'b1), .Q(register_4_q), .clk(clock_1_out));  // open: clr
  CIRCUIT_THREE circuit_three_1 (
    .in_1(register_3_q), .funct3_14_12(circuit_three_1_funct3_14_12), .out_5(circuit_three_1_out_5),
    .out_6(circuit_three_1_out_6), .RD_11_7(circuit_three_1_rd_11_7), ._6_0__OP(circuit_three_1__6_0__op),
    .funct7_5(circuit_three_1_funct7_5));
  Clock clock_2 (.out(clock_2_out));
  FSM fsm_1 (
    .ZERO(alu_1_zero), .OPCODE(circuit_three_1__6_0__op), .in_5(circuit_three_1_funct3_14_12),
    .in_6(circuit_three_1_funct7_5), .PCWrite(fsm_1_pcwrite), .out_8(fsm_1_out_8), .out_9(fsm_1_out_9),
    .out_10(fsm_1_out_10), .out_11(fsm_1_out_11), .out_12(fsm_1_out_12), .out_13(fsm_1_out_13),
    .out_14(fsm_1_out_14), .out_15(fsm_1_out_15), .out_16(fsm_1_out_16), .in_1(clock_2_out), .in_2(1'b0));
  // Probe on multiplexer_4_out
  Clock clock_3 (.out(clock_3_out));
  RegisterFile_32x32__2_read_1_write registerfile_32x32_2_read_1_write_1 (
    .Rs1(circuit_three_1_out_5), .Rs2(circuit_three_1_out_6), .Rd(circuit_three_1_rd_11_7),
    .out_7(registerfile_32x32_2_read_1_write_1_out_7), .out_8(registerfile_32x32_2_read_1_write_1_out_8),
    .R__Write(fsm_1_out_8), .clk(clock_3_out), .in_6(multiplexer_4_out));
  Extend extend_1 (.in_2(register_3_q), .out_3(extend_1_out_3), .ImmSrc(fsm_1_out_16));
  Clock clock_4 (.out(clock_4_out));
  Register #(.width(32)) register_5 (
    .D(registerfile_32x32_2_read_1_write_1_out_7), .Q(register_5_q), .clk(clock_4_out));  // open: en, clr
  Register #(.width(32)) register_6 (
    .D(registerfile_32x32_2_read_1_write_1_out_8), .Q(register_6_q), .clk(clock_4_out));  // open: en, clr
  Multiplexer #(.select(2), .width(32), .enable("false")) multiplexer_2 (
    .in0(register_1_q), .in1(register_2_q), .in2(register_5_q), .in3(undriven), .out(multiplexer_2_out),
    .sel(fsm_1_out_13));
  Multiplexer #(.select(2), .width(32), .enable("false")) multiplexer_3 (
    .in0(register_6_q), .in1(extend_1_out_3), .in2(32'h1), .out(multiplexer_3_out), .sel(fsm_1_out_12));  // open: in3
  // Probe on undriven_2
  ALU alu_1 (
    .in_2(multiplexer_2_out), .in_3(multiplexer_3_out), .ALUCtrl(fsm_1_out_15), .out_5(alu_1_out_5),
    .zero(alu_1_zero));
  Register #(.width(32)) register_7 (.D(alu_1_out_5), .Q(register_7_q), .clk(clock_5_out));  // open: en, clr
  Clock clock_5 (.out(clock_5_out));
  Multiplexer #(.select(2), .width(32), .enable("false")) multiplexer_4 (
    .in0(register_7_q), .in1(register_4_q), .in2(alu_1_out_5), .out(multiplexer_4_out), .sel(fsm_1_out_11));  // open: in3

  // Notes on the sheet:
  //   PC
  //   CIRCUIT THREE
  //   EXTEND
  //   SrcA
  //   SrcB
  //   ALU
endmodule

module LSED (
  input  [3:0] PCadd,
  input  [2:0] CtrlAddr,
  input  [6:0] OPCODE,
  output [3:0] mPcNext
);

  wire [3:0] dispatch_1_1_dispatch_1, dispatch_2_1_dispatch_2;

  DISPATCH_1 dispatch_1_1 (
    .in_1(4'b0111), .in_5(4'b0100), .Dispatch_1(dispatch_1_1_dispatch_1), .in_4(4'b0101), .in_3(4'b0010),
    .in_2(4'b0011), .in_6(OPCODE));
  DISPATCH_2 dispatch_2_1 (.in_1(4'b1001), .in_2(4'b1000), .in_3(OPCODE), .Dispatch_2(dispatch_2_1_dispatch_2));
  Multiplexer #(.select(3), .width(4), .enable("false")) multiplexer_1 (
    .in0(PCadd), .in1(4'b0000), .in2(dispatch_1_1_dispatch_1), .in3(dispatch_2_1_dispatch_2), .in4(4'b0110),
    .out(mPcNext), .sel(CtrlAddr));  // open: in5, in6, in7
endmodule

module DISPATCH_1 (
  input  [3:0] in_1,
  input  [3:0] in_2,
  input  [3:0] in_3,
  input  [3:0] in_4,
  input  [3:0] in_5,
  input  [6:0] in_6,
  output [3:0] Dispatch_1
);

  wire [3:0] MUX_0, MUX_4, MUX_27;

  Multiplexer #(.select(2), .width(4), .enable("false")) multiplexer_1 (
    .in0(in_1), .in1(in_1), .in3(in_3), .out(MUX_0), .sel(in_6[6:5]));  // open: in2
  Multiplexer #(.select(2), .width(4), .enable("false")) multiplexer_2 (
    .in3(in_2), .out(MUX_27), .sel(in_6[6:5]));  // open: in0, in1, in2
  Multiplexer #(.select(2), .width(4), .enable("false")) multiplexer_3 (
    .in0(in_5), .in1(in_4), .out(MUX_4), .sel(in_6[6:5]));  // open: in2, in3
  Multiplexer #(.select(5), .width(4), .enable("false")) multiplexer_4 (
    .in3(MUX_0), .in15(MUX_27), .in19(MUX_4), .out(Dispatch_1), .sel(in_6[4:0]));  // open: in0, in1, in2, in4, in5, in6, in7, in8, in9, in10, in11, in12, in13, in14, in16, in17, in18, in20, in21, in22, in23, in24, in25, in26, in27, in28, in29, in30, in31

  // Other names for the same wires on the sheet: S2__4_b0111[3:0] = in_1; S6_4_b0101[3:0] = in_4;
  //   S8_4_b0100[3:0] = in_5; S9_4_b0011[3:0] = in_2; S10_4_prime_0010[3:0] = in_3
endmodule

module DISPATCH_2 (
  input  [3:0] in_1,
  input  [3:0] in_2,
  input  [6:0] in_3,
  output [3:0] Dispatch_2
);

  wire [3:0] multiplexer_1_out;

  Multiplexer #(.select(2), .width(4), .enable("false")) multiplexer_1 (
    .in0(in_1), .in1(in_2), .out(multiplexer_1_out), .sel(in_3[6:5]));  // open: in2, in3
  Multiplexer #(.select(5), .width(4), .enable("false")) multiplexer_2 (
    .in3(multiplexer_1_out), .out(Dispatch_2), .sel(in_3[4:0]));  // open: in0, in1, in2, in4, in5, in6, in7, in8, in9, in10, in11, in12, in13, in14, in15, in16, in17, in18, in19, in20, in21, in22, in23, in24, in25, in26, in27, in28, in29, in30, in31

  // Other names for the same wires on the sheet: S3__4_b1001[3:0] = in_2; S5_4b_prime_1000[3:0] = in_1
endmodule

module FSM_main (
  input  in_1,
  input  in_2,
  input  [6:0] in_3,
  output out_4,
  output out_5,
  output out_6,
  output out_7,
  output out_8,
  output [1:0] out_9,
  output [1:0] out_10,
  output [1:0] out_11,
  output out_12,
  output [1:0] out_13
);

  wire clock_1_out;
  wire [2:0] rom_1_data;
  wire [3:0] adder_1_out, lsed_1_mpcnext, register_1_q;

  Adder #(.width(4)) adder_1 (.a(register_1_q), .b(4'b0001), .out(adder_1_out));  // open: cin, cout
  // Probe on register_1_q
  Register #(.width(4)) register_1 (.D(lsed_1_mpcnext), .Q(register_1_q), .clk(in_2), .clr(in_1));  // open: en
  Clock clock_1 (.out(clock_1_out));
  LSED lsed_1 (.PCadd(adder_1_out), .CtrlAddr(rom_1_data), .OPCODE(in_3), .mPcNext(lsed_1_mpcnext));
  ROM #(.addrWidth(4), .dataWidth(17)) rom_1 (
    .addr(register_1_q),
    .data({out_4, out_5, out_6, out_7, out_8, out_9, out_10, out_11, out_12, out_13, rom_1_data}), .sel(1'b1));
  // Probe on rom_1_data[2]
  // Probe on rom_1_data[0]
  // Probe on rom_1_data[1]
  // Probe on out_13[0]
  // Probe on out_13[1]
  // Probe on out_12
  // Probe on out_11[0]
  // Probe on out_11[1]
  // Probe on out_10[0]
  // Probe on out_10[1]
  // Probe on out_9[0]
  // Probe on out_9[1]
  // Probe on out_8
  // Probe on out_7
  // Probe on out_6
  // Probe on out_5
  // Probe on out_4

  // Notes on the sheet:
  //   PcAdd
  //   mPC
  //   contents of rom_1 (hex, n*v repeats v):
  //   9a00 142 10089 8244 194 94 4001 183 2021 20 4401
  //   CtrlAddr
  //   AdrSrc
  //   AluSrcA 1:0
  //   AluSrcB 1:0
  //   IRWrite
  //   MemoryWrite
  //   RegisterWrite
  //   PCUpdate
  //   branch
  //   ALUOp 1:0
  //   ResultSrc 1:0
endmodule

module InstrDecoder (
  input  [6:0] in_1,
  output [1:0] ImmSrc_1_0
);

  wire [1:0] MUX_00, MUX_01, MUX_02, R_type_4_bXX;

  Multiplexer #(.select(2), .width(2), .enable("false")) multiplexer_1 (
    .in0(2'b00), .in1(2'b01), .in3(2'b10), .out(MUX_00), .sel(in_1[6:5]));  // open: in2
  Multiplexer #(.select(2), .width(2), .enable("false")) multiplexer_2 (
    .in0(2'b00), .in3(R_type_4_bXX), .out(MUX_01), .sel(in_1[6:5]));  // open: in1, in2
  Multiplexer #(.select(2), .width(2), .enable("false")) multiplexer_3 (
    .in3(2'b11), .out(MUX_02), .sel(in_1[6:5]));  // open: in0, in1, in2
  Multiplexer #(.select(5), .width(2), .enable("false")) multiplexer_4 (
    .in3(MUX_00), .in15(MUX_02), .in19(MUX_01), .out(ImmSrc_1_0), .sel(in_1[4:0]));  // open: in0, in1, in2, in4, in5, in6, in7, in8, in9, in10, in11, in12, in13, in14, in16, in17, in18, in20, in21, in22, in23, in24, in25, in26, in27, in28, in29, in30, in31

  // Notes on the sheet:
  //   xx
endmodule

module FSM (
  input  in_1,
  input  in_2,
  input  ZERO,
  input  [6:0] OPCODE,
  input  [2:0] in_5,
  input  in_6,
  output PCWrite,
  output out_8,
  output out_9,
  output out_10,
  output [1:0] out_11,
  output [1:0] out_12,
  output [1:0] out_13,
  output out_14,
  output [2:0] out_15,
  output [1:0] out_16
);

  wire and_1_out, fsm_main_1_out_4, fsm_main_1_out_5;
  wire [1:0] fsm_main_1_out_13;

  Clock clock_1 ();  // open: out
  FSM_main fsm_main_1 (
    .out_5(fsm_main_1_out_5), .out_4(fsm_main_1_out_4), .out_6(out_8), .out_7(out_9), .out_8(out_10),
    .out_9(out_11), .out_10(out_12), .out_11(out_13), .out_12(out_14), .out_13(fsm_main_1_out_13),
    .in_3(OPCODE), .in_2(in_1), .in_1(in_2));
  ALUDecoder aludecoder_1 (
    .ALUControl(out_15), .in_1(OPCODE[5]), .in_2(in_6), .funct3(in_5), .aluop(fsm_main_1_out_13));
  InstrDecoder instrdecoder_1 (.in_1(OPCODE), .ImmSrc_1_0(out_16));
  and and_1 (and_1_out, ZERO, fsm_main_1_out_4);
  or or_1 (PCWrite, and_1_out, fsm_main_1_out_5);
endmodule

module ALUDecoder (
  input  in_1,
  input  in_2,
  input  [1:0] aluop,
  input  [2:0] funct3,
  output [2:0] ALUControl
);

  wire [2:0] multiplexer_1_out, multiplexer_2_out;

  Multiplexer #(.select(2), .width(3), .enable("false")) multiplexer_1 (
    .in0(3'b000), .in1(3'b000), .in2(3'b000), .in3(3'b001), .out(multiplexer_1_out), .sel({in_1, in_2}));
  Multiplexer #(.select(3), .width(3), .enable("false")) multiplexer_2 (
    .in0(multiplexer_1_out), .in2(3'b010), .in3(3'b101), .in6(3'b011), .in7(3'b010), .out(multiplexer_2_out),
    .sel(funct3));  // open: in1, in4, in5
  Multiplexer #(.select(2), .width(3), .enable("false")) multiplexer_3 (
    .in0(3'b000), .in1(3'b001), .in2(multiplexer_2_out), .out(ALUControl), .sel(aluop));  // open: in3

  // Notes on the sheet:
  //   op 5, funct7 5
endmodule

module RegisterFile_32x32__2_read_1_write (
  input  R__Write,
  input  clk,
  input  [4:0] Rs1,
  input  [4:0] Rs2,
  input  [4:0] Rd,
  input  [31:0] in_6,
  output [31:0] out_7,
  output [31:0] out_8
);

  _1_bit_reg_file u_1_bit_reg_file_1 (
    .clk(clk), .Reg0_in(Rs1), .Reg1_in(Rs2), .in_4(Rd), .in_5(in_6[0]), .Write_Enable(R__Write),
    .Reg0_out(out_7[0]), .out_8(out_8[0]));
  _1_bit_reg_file u_1_bit_reg_file_2 (
    .clk(clk), .Reg0_in(Rs1), .Reg1_in(Rs2), .in_4(Rd), .in_5(in_6[1]), .Write_Enable(R__Write),
    .Reg0_out(out_7[1]), .out_8(out_8[1]));
  _1_bit_reg_file u_1_bit_reg_file_3 (
    .clk(clk), .Reg0_in(Rs1), .Reg1_in(Rs2), .in_4(Rd), .in_5(in_6[2]), .Write_Enable(R__Write),
    .Reg0_out(out_7[2]), .out_8(out_8[2]));
  _1_bit_reg_file u_1_bit_reg_file_4 (
    .clk(clk), .Reg0_in(Rs1), .Reg1_in(Rs2), .in_4(Rd), .in_5(in_6[3]), .Write_Enable(R__Write),
    .Reg0_out(out_7[3]), .out_8(out_8[3]));
  _1_bit_reg_file u_1_bit_reg_file_5 (
    .clk(clk), .Reg0_in(Rs1), .Reg1_in(Rs2), .in_4(Rd), .in_5(in_6[4]), .Write_Enable(R__Write),
    .Reg0_out(out_7[4]), .out_8(out_8[4]));
  _1_bit_reg_file u_1_bit_reg_file_6 (
    .clk(clk), .Reg0_in(Rs1), .Reg1_in(Rs2), .in_4(Rd), .in_5(in_6[5]), .Write_Enable(R__Write),
    .Reg0_out(out_7[5]), .out_8(out_8[5]));
  _1_bit_reg_file u_1_bit_reg_file_7 (
    .clk(clk), .Reg0_in(Rs1), .Reg1_in(Rs2), .in_4(Rd), .in_5(in_6[6]), .Write_Enable(R__Write),
    .Reg0_out(out_7[6]), .out_8(out_8[6]));
  _1_bit_reg_file u_1_bit_reg_file_8 (
    .clk(clk), .Reg0_in(Rs1), .Reg1_in(Rs2), .in_4(Rd), .in_5(in_6[7]), .Write_Enable(R__Write),
    .Reg0_out(out_7[7]), .out_8(out_8[7]));
  _1_bit_reg_file u_1_bit_reg_file_9 (
    .clk(clk), .Reg0_in(Rs1), .Reg1_in(Rs2), .in_4(Rd), .in_5(in_6[8]), .Write_Enable(R__Write),
    .Reg0_out(out_7[8]), .out_8(out_8[8]));
  _1_bit_reg_file u_1_bit_reg_file_10 (
    .clk(clk), .Reg0_in(Rs1), .Reg1_in(Rs2), .in_4(Rd), .in_5(in_6[11]), .Write_Enable(R__Write),
    .Reg0_out(out_7[9]), .out_8(out_8[9]));
  _1_bit_reg_file u_1_bit_reg_file_11 (
    .clk(clk), .Reg0_in(Rs1), .Reg1_in(Rs2), .in_4(Rd), .in_5(in_6[9]), .Write_Enable(R__Write),
    .Reg0_out(out_7[10]), .out_8(out_8[10]));
  _1_bit_reg_file u_1_bit_reg_file_12 (
    .clk(clk), .Reg0_in(Rs1), .Reg1_in(Rs2), .in_4(Rd), .in_5(in_6[10]), .Write_Enable(R__Write),
    .Reg0_out(out_7[11]), .out_8(out_8[11]));
  _1_bit_reg_file u_1_bit_reg_file_13 (
    .clk(clk), .Reg0_in(Rs1), .Reg1_in(Rs2), .in_4(Rd), .in_5(in_6[12]), .Write_Enable(R__Write),
    .Reg0_out(out_7[12]), .out_8(out_8[12]));
  _1_bit_reg_file u_1_bit_reg_file_14 (
    .clk(clk), .Reg0_in(Rs1), .Reg1_in(Rs2), .in_4(Rd), .in_5(in_6[13]), .Write_Enable(R__Write),
    .Reg0_out(out_7[13]), .out_8(out_8[13]));
  _1_bit_reg_file u_1_bit_reg_file_15 (
    .clk(clk), .Reg0_in(Rs1), .Reg1_in(Rs2), .in_4(Rd), .in_5(in_6[14]), .Write_Enable(R__Write),
    .Reg0_out(out_7[14]), .out_8(out_8[14]));
  _1_bit_reg_file u_1_bit_reg_file_16 (
    .clk(clk), .Reg0_in(Rs1), .Reg1_in(Rs2), .in_4(Rd), .in_5(in_6[15]), .Write_Enable(R__Write),
    .Reg0_out(out_7[15]), .out_8(out_8[15]));
  _1_bit_reg_file u_1_bit_reg_file_17 (
    .clk(clk), .Reg0_in(Rs1), .Reg1_in(Rs2), .in_4(Rd), .in_5(in_6[16]), .Write_Enable(R__Write),
    .Reg0_out(out_7[16]), .out_8(out_8[16]));
  _1_bit_reg_file u_1_bit_reg_file_18 (
    .clk(clk), .Reg0_in(Rs1), .Reg1_in(Rs2), .in_4(Rd), .in_5(in_6[17]), .Write_Enable(R__Write),
    .Reg0_out(out_7[17]), .out_8(out_8[17]));
  _1_bit_reg_file u_1_bit_reg_file_19 (
    .clk(clk), .Reg0_in(Rs1), .Reg1_in(Rs2), .in_4(Rd), .in_5(in_6[18]), .Write_Enable(R__Write),
    .Reg0_out(out_7[18]), .out_8(out_8[18]));
  _1_bit_reg_file u_1_bit_reg_file_20 (
    .clk(clk), .Reg0_in(Rs1), .Reg1_in(Rs2), .in_4(Rd), .in_5(in_6[19]), .Write_Enable(R__Write),
    .Reg0_out(out_7[19]), .out_8(out_8[19]));
  _1_bit_reg_file u_1_bit_reg_file_21 (
    .clk(clk), .Reg0_in(Rs1), .Reg1_in(Rs2), .in_4(Rd), .in_5(in_6[20]), .Write_Enable(R__Write),
    .Reg0_out(out_7[20]), .out_8(out_8[20]));
  _1_bit_reg_file u_1_bit_reg_file_22 (
    .clk(clk), .Reg0_in(Rs1), .Reg1_in(Rs2), .in_4(Rd), .in_5(in_6[21]), .Write_Enable(R__Write),
    .Reg0_out(out_7[21]), .out_8(out_8[21]));
  _1_bit_reg_file u_1_bit_reg_file_23 (
    .clk(clk), .Reg0_in(Rs1), .Reg1_in(Rs2), .in_4(Rd), .in_5(in_6[22]), .Write_Enable(R__Write),
    .Reg0_out(out_7[22]), .out_8(out_8[22]));
  _1_bit_reg_file u_1_bit_reg_file_24 (
    .clk(clk), .Reg0_in(Rs1), .Reg1_in(Rs2), .in_4(Rd), .in_5(in_6[23]), .Write_Enable(R__Write),
    .Reg0_out(out_7[23]), .out_8(out_8[23]));
  _1_bit_reg_file u_1_bit_reg_file_25 (
    .clk(clk), .Reg0_in(Rs1), .Reg1_in(Rs2), .in_4(Rd), .in_5(in_6[24]), .Write_Enable(R__Write),
    .Reg0_out(out_7[24]), .out_8(out_8[24]));
  _1_bit_reg_file u_1_bit_reg_file_26 (
    .clk(clk), .Reg0_in(Rs1), .Reg1_in(Rs2), .in_4(Rd), .in_5(in_6[25]), .Write_Enable(R__Write),
    .Reg0_out(out_7[25]), .out_8(out_8[25]));
  _1_bit_reg_file u_1_bit_reg_file_27 (
    .clk(clk), .Reg0_in(Rs1), .Reg1_in(Rs2), .in_4(Rd), .in_5(in_6[26]), .Write_Enable(R__Write),
    .Reg0_out(out_7[26]), .out_8(out_8[26]));
  _1_bit_reg_file u_1_bit_reg_file_28 (
    .clk(clk), .Reg0_in(Rs1), .Reg1_in(Rs2), .in_4(Rd), .in_5(in_6[27]), .Write_Enable(R__Write),
    .Reg0_out(out_7[27]), .out_8(out_8[27]));
  _1_bit_reg_file u_1_bit_reg_file_29 (
    .clk(clk), .Reg0_in(Rs1), .Reg1_in(Rs2), .in_4(Rd), .in_5(in_6[28]), .Write_Enable(R__Write),
    .Reg0_out(out_7[28]), .out_8(out_8[28]));
  _1_bit_reg_file u_1_bit_reg_file_30 (
    .clk(clk), .Reg0_in(Rs1), .Reg1_in(Rs2), .in_4(Rd), .in_5(in_6[29]), .Write_Enable(R__Write),
    .Reg0_out(out_7[29]), .out_8(out_8[29]));
  _1_bit_reg_file u_1_bit_reg_file_31 (
    .clk(clk), .Reg0_in(Rs1), .Reg1_in(Rs2), .in_4(Rd), .in_5(in_6[30]), .Write_Enable(R__Write),
    .Reg0_out(out_7[30]), .out_8(out_8[30]));
  _1_bit_reg_file u_1_bit_reg_file_32 (
    .clk(clk), .Reg0_in(Rs1), .Reg1_in(Rs2), .in_4(Rd), .in_5(in_6[31]), .Write_Enable(R__Write),
    .Reg0_out(out_7[31]), .out_8(out_8[31]));

  // Notes on the sheet:
  //   DATA
  //   Rd1
  //   Rd2
endmodule

module _1_bit_reg_file (
  input  clk,
  input  [4:0] Reg0_in,
  input  [4:0] Reg1_in,
  input  [4:0] in_4,
  input  in_5,
  input  Write_Enable,
  output Reg0_out,
  output out_8
);

  wire and_1_out, and_2_out, and_3_out, and_4_out, and_5_out, and_6_out, and_7_out, and_8_out, and_9_out,
       and_10_out, and_11_out, and_12_out, and_13_out, and_14_out, and_15_out, and_16_out, and_17_out,
       and_18_out, and_19_out, and_20_out, and_21_out, and_22_out, and_23_out, and_24_out, and_25_out,
       and_26_out, and_27_out, and_28_out, and_29_out, and_30_out, and_31_out, and_32_out, d_ff_2_q,
       d_ff_3_q, d_ff_4_q, d_ff_5_q, d_ff_6_q, d_ff_7_q, d_ff_8_q, d_ff_9_q, d_ff_10_q, d_ff_11_q, d_ff_12_q,
       d_ff_13_q, d_ff_14_q, d_ff_15_q, d_ff_16_q, d_ff_17_q, d_ff_18_q, d_ff_19_q, d_ff_20_q, d_ff_21_q,
       d_ff_22_q, d_ff_23_q, d_ff_24_q, d_ff_25_q, d_ff_26_q, d_ff_27_q, d_ff_28_q, d_ff_29_q, d_ff_30_q,
       d_ff_31_q, d_ff_32_q, decoder_1_out0, decoder_1_out1, decoder_1_out2, decoder_1_out3, decoder_1_out4,
       decoder_1_out5, decoder_1_out6, decoder_1_out7, decoder_1_out8, decoder_1_out9, decoder_1_out10,
       decoder_1_out11, decoder_1_out12, decoder_1_out13, decoder_1_out14, decoder_1_out15, decoder_1_out16,
       decoder_1_out17, decoder_1_out18, decoder_1_out19, decoder_1_out20, decoder_1_out21, decoder_1_out22,
       decoder_1_out23, decoder_1_out24, decoder_1_out25, decoder_1_out26, decoder_1_out27, decoder_1_out28,
       decoder_1_out29, decoder_1_out30, decoder_1_out31;

  Decoder #(.select(5), .enable("false")) decoder_1 (
    .out0(decoder_1_out0), .out1(decoder_1_out1), .out2(decoder_1_out2), .out3(decoder_1_out3),
    .out4(decoder_1_out4), .out5(decoder_1_out5), .out6(decoder_1_out6), .out7(decoder_1_out7),
    .out8(decoder_1_out8), .out9(decoder_1_out9), .out10(decoder_1_out10), .out11(decoder_1_out11),
    .out12(decoder_1_out12), .out13(decoder_1_out13), .out14(decoder_1_out14), .out15(decoder_1_out15),
    .out16(decoder_1_out16), .out17(decoder_1_out17), .out18(decoder_1_out18), .out19(decoder_1_out19),
    .out20(decoder_1_out20), .out21(decoder_1_out21), .out22(decoder_1_out22), .out23(decoder_1_out23),
    .out24(decoder_1_out24), .out25(decoder_1_out25), .out26(decoder_1_out26), .out27(decoder_1_out27),
    .out28(decoder_1_out28), .out29(decoder_1_out29), .out30(decoder_1_out30), .out31(decoder_1_out31),
    .sel(in_4));
  and and_1 (and_1_out, decoder_1_out0, clk, Write_Enable);
  and and_2 (and_2_out, decoder_1_out1, clk, Write_Enable);
  and and_3 (and_3_out, decoder_1_out2, clk, Write_Enable);
  and and_4 (and_4_out, decoder_1_out3, clk, Write_Enable);
  and and_5 (and_5_out, decoder_1_out4, clk, Write_Enable);
  and and_6 (and_6_out, decoder_1_out5, clk, Write_Enable);
  and and_7 (and_7_out, decoder_1_out6, clk, Write_Enable);
  and and_8 (and_8_out, decoder_1_out7, clk, Write_Enable);
  and and_9 (and_9_out, decoder_1_out8, clk, Write_Enable);
  and and_10 (and_10_out, decoder_1_out9, clk, Write_Enable);
  and and_11 (and_11_out, decoder_1_out10, clk, Write_Enable);
  and and_12 (and_12_out, decoder_1_out11, clk, Write_Enable);
  and and_13 (and_13_out, decoder_1_out12, clk, Write_Enable);
  and and_14 (and_14_out, decoder_1_out13, clk, Write_Enable);
  and and_15 (and_15_out, decoder_1_out14, clk, Write_Enable);
  and and_16 (and_16_out, decoder_1_out15, clk, Write_Enable);
  and and_17 (and_17_out, decoder_1_out16, clk, Write_Enable);
  and and_18 (and_18_out, decoder_1_out17, clk, Write_Enable);
  and and_19 (and_19_out, decoder_1_out18, clk, Write_Enable);
  and and_20 (and_20_out, decoder_1_out19, clk, Write_Enable);
  and and_21 (and_21_out, decoder_1_out20, clk, Write_Enable);
  and and_22 (and_22_out, decoder_1_out21, clk, Write_Enable);
  and and_23 (and_23_out, decoder_1_out22, clk, Write_Enable);
  and and_24 (and_24_out, decoder_1_out23, clk, Write_Enable);
  and and_25 (and_25_out, decoder_1_out24, clk, Write_Enable);
  and and_26 (and_26_out, decoder_1_out25, clk, Write_Enable);
  and and_27 (and_27_out, decoder_1_out26, clk, Write_Enable);
  and and_28 (and_28_out, decoder_1_out27, clk, Write_Enable);
  and and_29 (and_29_out, decoder_1_out28, clk, Write_Enable);
  and and_30 (and_30_out, decoder_1_out29, clk, Write_Enable);
  and and_31 (and_31_out, decoder_1_out30, clk, Write_Enable);
  and and_32 (and_32_out, decoder_1_out31, clk, Write_Enable);
  D_Flip_Flop #(.trigger("high")) d_ff_1 (.clk(and_1_out), .D(in_5));  // open: Q, Qn, preset, en, reset
  D_Flip_Flop d_ff_2 (.clk(and_2_out), .D(in_5), .Q(d_ff_2_q));  // open: Qn, preset, en, reset
  D_Flip_Flop d_ff_3 (.clk(and_3_out), .D(in_5), .Q(d_ff_3_q));  // open: Qn, preset, en, reset
  D_Flip_Flop d_ff_4 (.clk(and_4_out), .D(in_5), .Q(d_ff_4_q));  // open: Qn, preset, en, reset
  D_Flip_Flop d_ff_5 (.clk(and_5_out), .D(in_5), .Q(d_ff_5_q));  // open: Qn, preset, en, reset
  D_Flip_Flop d_ff_6 (.clk(and_6_out), .D(in_5), .Q(d_ff_6_q));  // open: Qn, preset, en, reset
  D_Flip_Flop d_ff_7 (.clk(and_7_out), .D(in_5), .Q(d_ff_7_q));  // open: Qn, preset, en, reset
  D_Flip_Flop d_ff_8 (.clk(and_8_out), .D(in_5), .Q(d_ff_8_q));  // open: Qn, preset, en, reset
  D_Flip_Flop d_ff_9 (.clk(and_9_out), .D(in_5), .Q(d_ff_9_q));  // open: Qn, preset, en, reset
  D_Flip_Flop d_ff_10 (.clk(and_10_out), .D(in_5), .Q(d_ff_10_q));  // open: Qn, preset, en, reset
  D_Flip_Flop d_ff_11 (.clk(and_11_out), .D(in_5), .Q(d_ff_11_q));  // open: Qn, preset, en, reset
  D_Flip_Flop d_ff_12 (.clk(and_12_out), .D(in_5), .Q(d_ff_12_q));  // open: Qn, preset, en, reset
  D_Flip_Flop d_ff_13 (.clk(and_13_out), .D(in_5), .Q(d_ff_13_q));  // open: Qn, preset, en, reset
  D_Flip_Flop d_ff_14 (.clk(and_14_out), .D(in_5), .Q(d_ff_14_q));  // open: Qn, preset, en, reset
  D_Flip_Flop d_ff_15 (.clk(and_15_out), .D(in_5), .Q(d_ff_15_q));  // open: Qn, preset, en, reset
  D_Flip_Flop d_ff_16 (.clk(and_16_out), .D(in_5), .Q(d_ff_16_q));  // open: Qn, preset, en, reset
  D_Flip_Flop d_ff_17 (.clk(and_17_out), .D(in_5), .Q(d_ff_17_q));  // open: Qn, preset, en, reset
  D_Flip_Flop d_ff_18 (.clk(and_18_out), .D(in_5), .Q(d_ff_18_q));  // open: Qn, preset, en, reset
  D_Flip_Flop d_ff_19 (.clk(and_19_out), .D(in_5), .Q(d_ff_19_q));  // open: Qn, preset, en, reset
  D_Flip_Flop d_ff_20 (.clk(and_20_out), .D(in_5), .Q(d_ff_20_q));  // open: Qn, preset, en, reset
  D_Flip_Flop d_ff_21 (.clk(and_21_out), .D(in_5), .Q(d_ff_21_q));  // open: Qn, preset, en, reset
  D_Flip_Flop d_ff_22 (.clk(and_22_out), .D(in_5), .Q(d_ff_22_q));  // open: Qn, preset, en, reset
  D_Flip_Flop d_ff_23 (.clk(and_23_out), .D(in_5), .Q(d_ff_23_q));  // open: Qn, preset, en, reset
  D_Flip_Flop d_ff_24 (.clk(and_24_out), .D(in_5), .Q(d_ff_24_q));  // open: Qn, preset, en, reset
  D_Flip_Flop d_ff_25 (.clk(and_25_out), .D(in_5), .Q(d_ff_25_q));  // open: Qn, preset, en, reset
  D_Flip_Flop d_ff_26 (.clk(and_26_out), .D(in_5), .Q(d_ff_26_q));  // open: Qn, preset, en, reset
  D_Flip_Flop d_ff_27 (.clk(and_27_out), .D(in_5), .Q(d_ff_27_q));  // open: Qn, preset, en, reset
  D_Flip_Flop d_ff_28 (.clk(and_28_out), .D(in_5), .Q(d_ff_28_q));  // open: Qn, preset, en, reset
  D_Flip_Flop d_ff_29 (.clk(and_29_out), .D(in_5), .Q(d_ff_29_q));  // open: Qn, preset, en, reset
  D_Flip_Flop d_ff_30 (.clk(and_30_out), .D(in_5), .Q(d_ff_30_q));  // open: Qn, preset, en, reset
  D_Flip_Flop d_ff_31 (.clk(and_31_out), .D(in_5), .Q(d_ff_31_q));  // open: Qn, preset, en, reset
  D_Flip_Flop d_ff_32 (.clk(and_32_out), .D(in_5), .Q(d_ff_32_q));  // open: Qn, preset, en, reset
  Multiplexer #(.select(5), .enable("false")) multiplexer_1 (
    .in0(1'b0), .in1(d_ff_2_q), .in2(d_ff_3_q), .in3(d_ff_4_q), .in4(d_ff_5_q), .in5(d_ff_6_q),
    .in6(d_ff_7_q), .in7(d_ff_8_q), .in8(d_ff_9_q), .in9(d_ff_10_q), .in10(d_ff_11_q), .in11(d_ff_12_q),
    .in12(d_ff_13_q), .in13(d_ff_14_q), .in14(d_ff_15_q), .in15(d_ff_16_q), .in16(d_ff_17_q),
    .in17(d_ff_18_q), .in18(d_ff_19_q), .in19(d_ff_20_q), .in20(d_ff_21_q), .in21(d_ff_22_q),
    .in22(d_ff_23_q), .in23(d_ff_24_q), .in24(d_ff_25_q), .in25(d_ff_26_q), .in26(d_ff_27_q),
    .in27(d_ff_28_q), .in28(d_ff_29_q), .in29(d_ff_30_q), .in30(d_ff_31_q), .in31(d_ff_32_q), .out(Reg0_out),
    .sel(Reg0_in));
  Multiplexer #(.select(5), .enable("false")) multiplexer_2 (
    .in0(1'b0), .in1(d_ff_2_q), .in2(d_ff_3_q), .in3(d_ff_4_q), .in4(d_ff_5_q), .in5(d_ff_6_q),
    .in6(d_ff_7_q), .in7(d_ff_8_q), .in8(d_ff_9_q), .in9(d_ff_10_q), .in10(d_ff_11_q), .in11(d_ff_12_q),
    .in12(d_ff_13_q), .in13(d_ff_14_q), .in14(d_ff_15_q), .in15(d_ff_16_q), .in16(d_ff_17_q),
    .in17(d_ff_18_q), .in18(d_ff_19_q), .in19(d_ff_20_q), .in20(d_ff_21_q), .in21(d_ff_22_q),
    .in22(d_ff_23_q), .in23(d_ff_24_q), .in24(d_ff_25_q), .in25(d_ff_26_q), .in26(d_ff_27_q),
    .in27(d_ff_28_q), .in28(d_ff_29_q), .in29(d_ff_30_q), .in30(d_ff_31_q), .in31(d_ff_32_q), .out(out_8),
    .sel(Reg1_in));

  // Notes on the sheet:
  //   i bit of write data for write port
endmodule

module CIRCUIT_THREE (
  input  [31:0] in_1,
  output [2:0] funct3_14_12,
  output funct7_5,
  output [6:0] _6_0__OP,
  output [4:0] out_5,
  output [4:0] out_6,
  output [4:0] RD_11_7
);


  assign _6_0__OP = in_1[6:0];
  assign funct3_14_12 = in_1[14:12];
  assign funct7_5 = in_1[30];
  assign out_5 = in_1[19:15];
  assign out_6 = in_1[24:20];
  assign RD_11_7 = in_1[11:7];

  // Notes on the sheet:
  //   Instr
  //   Rs1 19:15
  //   Rs2 24:20
endmodule

module Extend (
  input  [1:0] ImmSrc,
  input  [31:0] in_2,
  output [31:0] out_3
);

  wire [31:0] bit_extender_1_out, bit_extender_2_out, bit_extender_3_out, bit_extender_4_out;

  assign bit_extender_1_out = {{20{in_2[31]}}, in_2[31:20]};  // Bit_Extender bit_extender_1
  assign bit_extender_2_out = {{20{in_2[31]}}, {in_2[31:25], in_2[11:7]}};  // Bit_Extender bit_extender_2
  assign bit_extender_3_out = {{20{in_2[31]}}, {in_2[31], in_2[7], in_2[30:25], in_2[11:8]}};  // Bit_Extender bit_extender_3
  assign bit_extender_4_out = {{12{in_2[31]}}, {in_2[31], in_2[19:12], in_2[20], in_2[30:21]}};  // Bit_Extender bit_extender_4
  Multiplexer #(.select(2), .width(32), .enable("false")) multiplexer_1 (
    .in0(bit_extender_1_out), .in1(bit_extender_2_out), .in2(bit_extender_3_out), .in3(bit_extender_4_out),
    .out(out_3), .sel(ImmSrc));

  // Notes on the sheet:
  //   Instr
  //   Out
endmodule

module ALU (
  input  [2:0] ALUCtrl,
  input  [31:0] in_2,
  input  [31:0] in_3,
  output zero,
  output [31:0] out_5
);

  wire comparator_1_lt, not_1_out, not_2_out, not_3_out, not_4_out, not_5_out, not_6_out, not_7_out,
       not_8_out, not_9_out, not_10_out, not_11_out, not_12_out, not_13_out, not_14_out, not_15_out,
       not_16_out, not_17_out, not_18_out, not_19_out, not_20_out, not_21_out, not_22_out, not_23_out,
       not_24_out, not_25_out, not_26_out, not_27_out, not_28_out, not_29_out, not_30_out, not_31_out,
       not_32_out;
  wire [31:0] adder_1_out, and_1_out, bit_extender_1_out, or_1_out, subtractor_1_out, xnor_1_out;

  assign xnor_1_out = ~(32'h1 ^ 32'h1);  // XNOR_Gate xnor_1, 32 bits wide
  // Probe on xnor_1_out
  Adder #(.width(32)) adder_1 (.a(in_2), .b(in_3), .out(adder_1_out));  // open: cin, cout
  Subtractor #(.width(32)) subtractor_1 (.a(in_2), .b(in_3), .out(subtractor_1_out));  // open: bin, bout
  Comparator #(.width(32)) comparator_1 (.a(in_2), .b(in_3), .lt(comparator_1_lt));  // open: gt, eq
  assign or_1_out = in_2 | in_3;  // OR_Gate or_1, 32 bits wide
  assign and_1_out = in_2 & in_3;  // AND_Gate and_1, 32 bits wide
  not not_1 (not_1_out, out_5[0]);
  not not_2 (not_2_out, out_5[1]);
  not not_3 (not_3_out, out_5[2]);
  not not_4 (not_4_out, out_5[3]);
  not not_5 (not_5_out, out_5[4]);
  not not_6 (not_6_out, out_5[5]);
  not not_7 (not_7_out, out_5[6]);
  not not_8 (not_8_out, out_5[7]);
  not not_9 (not_9_out, out_5[8]);
  not not_10 (not_10_out, out_5[9]);
  not not_11 (not_11_out, out_5[10]);
  not not_12 (not_12_out, out_5[11]);
  not not_13 (not_13_out, out_5[12]);
  not not_14 (not_14_out, out_5[13]);
  not not_15 (not_15_out, out_5[14]);
  not not_16 (not_16_out, out_5[15]);
  not not_17 (not_17_out, out_5[16]);
  not not_18 (not_18_out, out_5[17]);
  not not_19 (not_19_out, out_5[18]);
  not not_20 (not_20_out, out_5[19]);
  not not_21 (not_21_out, out_5[20]);
  not not_22 (not_22_out, out_5[21]);
  not not_23 (not_23_out, out_5[22]);
  not not_24 (not_24_out, out_5[23]);
  not not_25 (not_25_out, out_5[24]);
  not not_26 (not_26_out, out_5[25]);
  not not_27 (not_27_out, out_5[26]);
  not not_28 (not_28_out, out_5[27]);
  not not_29 (not_29_out, out_5[28]);
  not not_30 (not_30_out, out_5[29]);
  not not_31 (not_31_out, out_5[30]);
  not not_32 (not_32_out, out_5[31]);
  assign bit_extender_1_out = {{31{1'b0}}, comparator_1_lt};  // Bit_Extender bit_extender_1
  Multiplexer #(.select(3), .width(32), .enable("false")) multiplexer_1 (
    .in0(adder_1_out), .in1(subtractor_1_out), .in2(and_1_out), .in3(or_1_out), .in5(bit_extender_1_out),
    .out(out_5), .sel(ALUCtrl));  // open: in4, in6, in7
  // Probe on out_5
  and and_2 (zero, not_1_out, not_2_out, not_3_out, not_4_out, not_5_out, not_6_out, not_7_out, not_8_out, not_9_out, not_10_out, not_11_out, not_12_out, not_13_out, not_14_out, not_15_out, not_16_out, not_17_out, not_18_out, not_19_out, not_20_out, not_21_out, not_22_out, not_23_out, not_24_out, not_25_out, not_26_out, not_27_out, not_28_out, not_29_out, not_30_out, not_31_out, not_32_out);

  // Notes on the sheet:
  //   SrcA
  //   SrcB
  //   ALU result
endmodule
